// Logisim project ACTUATE=IN_1+IN_2.circ as structural Verilog: 1 circuit, main circuit main
module main (
  input  IN1_L,
  input  IN2_L,
  input  SEL_H,
  input  DETECT_H,
  input  TNR_H,
  input  TOL_H,
  input  IN_,
  input  in_8,
  output out_9,
  output out_10,
  output out_11
);

  wire and_2_out, nand_1_out, not_1_out;

  or or_1 (out_9, IN1_L, IN2_L);
  and and_1 (out_11, SEL_H, DETECT_H);
  not not_1 (not_1_out, TNR_H);
  nand nand_1 (nand_1_out, not_1_out, not_1_out, TOL_H, IN_);
  xor xor_1 (out_10, out_9, out_11);
  and and_2 (and_2_out, nand_1_out, in_8);
  LED led_1 (.in(out_10));
  LED led_2 (.in(and_2_out));

  // Notes on the sheet:
  //   not_1 drives only 0 and floats otherwise
  //   nand_1 drives only 1 and floats otherwise
endmodule
