// Logisim project alarmeAUTO.circ as structural Verilog: 2 circuits, main circuit alarme_automovel
// Alarme
module alarme_automovel (
  input  F,
  input  M,
  input  P,
  input  C,
  output Alarme
);

  wire and_1_out, and_2_out, and_3_out, not_1_out, not_2_out, not_3_out;

  not not_1 (not_1_out, M);
  not not_2 (not_2_out, P);
  not not_3 (not_3_out, C);
  and and_1 (and_1_out, F, not_1_out);
  and and_2 (and_2_out, M, P);
  and and_3 (and_3_out, not_2_out, not_3_out, M);
  or or_1 (Alarme, and_1_out, and_2_out, and_3_out);
endmodule

module alarme_automovel_minizado (
  input  F,
  input  M,
  input  P,
  input  C,
  output Alarme
);

  wire and_1_out, and_2_out, and_3_out, not_1_out, not_2_out;

  and and_1 (and_1_out, M, not_1_out);
  not not_1 (not_1_out, C);
  and and_2 (and_2_out, M, P);
  and and_3 (and_3_out, F, not_2_out);
  not not_2 (not_2_out, M);
  or or_1 (Alarme, and_1_out, and_2_out, and_3_out);
endmodule
