// Logisim project 1-Alarme.circ as structural Verilog: 1 circuit, main circuit main
module main (
  input  Porta1,
  input  Porta2,
  input  Porta3,
  input  Porta4,
  input  Chave_Ignicao,
  input  Luzes,
  output ALARME
);

  wire and_1_out, and_2_out, not_1_out, not_2_out, or_1_out;

  or or_1 (or_1_out, Porta1, Porta2, Porta3, Porta4);
  not not_1 (not_1_out, Luzes);
  not not_2 (not_2_out, Chave_Ignicao);
  and and_1 (and_1_out, or_1_out, Chave_Ignicao);
  and and_2 (and_2_out, not_2_out, not_1_out);
  or or_2 (ALARME, and_1_out, and_2_out);

  // Notes on the sheet:
  //   ALARME: pull=up
endmodule
