// Logisim project 2-A).circ as structural Verilog: 1 circuit, main circuit main
module main (
  input  A_L,
  input  B_H,
  input  C_L,
  input  D_H,
  output Z_L
);

  wire not_1_out, not_2_out, not_3_out, or_1_out, or_2_out;

  not not_1 (not_1_out, A_L);
  not not_2 (not_2_out, B_H);
  not not_3 (not_3_out, C_L);
  or or_1 (or_1_out, not_1_out, not_2_out, not_3_out);
  or or_2 (or_2_out, not_2_out, D_H);
  nand nand_1 (Z_L, or_1_out, or_2_out);
endmodule
