// Logisim project 2-B).circ as structural Verilog: 1 circuit, main circuit main
module main (
  input  A_L,
  input  B_H,
  input  C_L,
  input  D_H,
  output Z_L
);

  wire nand_1_out, not_1_out, or_1_out;

  or or_1 (or_1_out, A_L, B_H, C_L);
  nand nand_1 (nand_1_out, C_L, D_H);
  not not_1 (not_1_out, nand_1_out);
  and and_1 (Z_L, or_1_out, not_1_out);
endmodule
