// Logisim project 2-C).circ as structural Verilog: 1 circuit, main circuit main
module main (
  input  A_L,
  input  B_H,
  input  C_L,
  input  D_H,
  output Z_L
);

  nor nor_1 (Z_L, A_L, B_H, C_L, D_H);
endmodule
