// Logisim project 3-G a M.circ as structural Verilog: 1 circuit, main circuit main
module main (
  input  INTERRUPTOR_ON_L,
  input  ACCAO_L,
  input  DESLIGAR_L,
  output RESULTADO_H
);

  wire and_1_out, not_1_out, not_2_out, not_3_out, not_4_out, or_1_out;

  not not_1 (not_1_out, ACCAO_L);
  not not_2 (not_2_out, INTERRUPTOR_ON_L);
  or or_1 (or_1_out, INTERRUPTOR_ON_L, not_1_out);
  and and_1 (and_1_out, not_2_out, DESLIGAR_L);
  not not_3 (not_3_out, or_1_out);
  not not_4 (not_4_out, not_3_out);
  and and_2 (RESULTADO_H, not_4_out, and_1_out);
endmodule
