// Logisim project 4-G a M.circ as structural Verilog: 1 circuit, main circuit main
module main (
  input  ACCAO1,
  input  ACCAO2,
  input  ACCAO3,
  output RESULTADO
);

  wire and_1_out;

  and and_1 (and_1_out, ACCAO1, ACCAO2);
  or or_1 (RESULTADO, and_1_out, ACCAO3);
endmodule
