// Logisim project 5-Elevador.circ as structural Verilog: 1 circuit, main circuit main
module main (
  input  ELEV_NO_PISO_INFERIOR_H,
  input  ELEV_NO_PISO_SUPERIOR_L,
  input  ELEV_A_SUBIR_H,
  input  ELEV_A_DESCER_L,
  input  PEDIDO_DE_SUBIDA_L,
  input  PEDIDO_DE_DESCIDA_L,
  input  PORTA_ABERTA_H,
  output MARCHA_ASCENDENTE_H,
  output MARCHA_DESCENDENTE_L,
  output PORTA_SUP_BLOQUEADA_L,
  output PORTA_INF_BLOQUEADA_H
);

  wire and_1_out, and_2_out, nand_1_out, nand_2_out, nand_3_out, nand_4_out, nand_5_out;

  nand nand_1 (nand_1_out, ELEV_NO_PISO_INFERIOR_H, ELEV_NO_PISO_SUPERIOR_L);
  nand nand_2 (nand_2_out, ELEV_A_SUBIR_H, ELEV_A_DESCER_L);
  nand nand_3 (nand_3_out, PEDIDO_DE_SUBIDA_L, PEDIDO_DE_DESCIDA_L);
  nand nand_4 (nand_4_out, ELEV_NO_PISO_INFERIOR_H, nand_1_out, ELEV_NO_PISO_SUPERIOR_L, PORTA_ABERTA_H);
  nand nand_5 (nand_5_out, nand_2_out, nand_3_out, PORTA_ABERTA_H);
  and and_1 (and_1_out, nand_5_out, nand_4_out);
  and and_2 (and_2_out, nand_5_out, nand_4_out);
  or or_1 (MARCHA_DESCENDENTE_L, and_1_out, and_2_out);
  not not_1 (MARCHA_ASCENDENTE_H, MARCHA_DESCENDENTE_L);
  not not_2 (PORTA_INF_BLOQUEADA_H, MARCHA_DESCENDENTE_L);

  assign PORTA_SUP_BLOQUEADA_L = MARCHA_DESCENDENTE_L;
endmodule
