// Logisim project Binario para BCD-3.circ as structural Verilog: 1 circuit, main circuit main
module main (
  input  [3:0] Bit_3,
  input  [3:0] Bit_2,
  input  [3:0] Bit_1,
  input  [3:0] Bit_0,
  output [3:0] Bit_3_2,
  output [3:0] Bit_2_2,
  output [3:0] Bit_1_2,
  output [3:0] Bit_0_2
);

  assign Bit_2_2 = Bit_3;  // XOR_Gate xor_1, 4 bits wide XOR_Gate
  assign Bit_1_2 = Bit_2;  // XOR_Gate xor_2, 4 bits wide XOR_Gate
  assign Bit_0_2 = Bit_1;  // XOR_Gate xor_3, 4 bits wide XOR_Gate

  assign Bit_3_2 = Bit_3;
endmodule
