// Logisim project Circuito Parte 1.circ as structural Verilog: 1 circuit, main circuit main
module main (
  input  [3:0] A0,
  input  [3:0] A1,
  input  [3:0] A2,
  input  [3:0] A3,
  input  [3:0] B0,
  input  [3:0] B1,
  input  [3:0] B2,
  input  [3:0] B3,
  input  [3:0] S1,
  input  [3:0] S2,
  input  [3:0] S3,
  input  [3:0] S4,
  input  [3:0] Cn0,
  input  [3:0] Cn1,
  input  [3:0] Cn2,
  input  [3:0] Cn3,
  input  [3:0] \Função_Correcao ,
  output [3:0] out_18,
  output CarryOut
);

  wire [3:0] adder_1_out, xor_1_out, xor_2_out, xor_3_out, xor_4_out, xor_5_out;

  ExactlyOne xor_1[3:0] (.out(xor_1_out), .in0(A0), .in1(A1), .in3(A2), .in4(A3));
  ExactlyOne xor_2[3:0] (.out(xor_2_out), .in0(B0), .in1(B1), .in3(B2), .in4(B3));
  ExactlyOne xor_3[3:0] (.out(xor_3_out), .in0(S1), .in1(S2), .in3(S3), .in4(S4));
  ExactlyOne xor_4[3:0] (.out(xor_4_out), .in0(Cn0), .in1(Cn1), .in3(Cn2), .in4(Cn3));
  Adder #(.width(4)) adder_1 (.a(xor_1_out), .b(xor_2_out), .out(adder_1_out), .cout(CarryOut));  // open: cin
  ExactlyOne xor_5[3:0] (.out(xor_5_out), .in0(adder_1_out), .in2(xor_3_out), .in4(xor_4_out));
  Adder #(.width(4)) adder_2 (.a(xor_5_out), .b(\Função_Correcao ), .out(out_18));  // open: cin, cout
endmodule
