// Logisim project Circuito Parte 2.circ as structural Verilog: 1 circuit, main circuit main
module main (
  input  in_1,
  input  in_2,
  input  in_3,
  input  in_4,
  input  Logica_de_Controle,
  input  RESET
);

  wire and_1_out, CLOCK_out, Q0_q, Q0_qn;

  Clock CLOCK (.out(CLOCK_out));
  D_Flip_Flop #(.trigger("falling")) Q3 (
    .clk(and_1_out), .D(in_1), .preset(Logica_de_Controle), .reset(RESET));  // open: Q, Qn, en
  D_Flip_Flop Q2 (.clk(CLOCK_out), .D(CLOCK_out), .preset(in_2), .reset(RESET));  // open: Q, Qn, en
  D_Flip_Flop Q1 (.clk(CLOCK_out), .D(in_3), .preset(in_3), .reset(RESET));  // open: Q, Qn, en
  D_Flip_Flop #(.trigger("falling")) Q0 (
    .clk(in_4), .Q(Q0_q), .Qn(Q0_qn), .preset(CLOCK_out), .reset(RESET));  // open: D, en
  and and_1 (and_1_out, CLOCK_out, Q0_q, Q0_qn);
endmodule
