// Logisim project Guidaste-1.circ as structural Verilog: 1 circuit, main circuit main
module main (
  input  \Lança_Elev_1 ,
  input  \Lança_Elev_2 ,
  input  \Lança_Abai_1 ,
  input  \Lança_Abai_2 ,
  input  Rodar_Esq_1,
  input  Rodar_Esq_2,
  input  Rodar_Dir_1,
  input  Rodar_Dir_2,
  input  Cabo_Des_1,
  input  Cabo_Des_2,
  input  Cabo_Enr_1,
  input  Cabo_Enr_2,
  input  Abrir_Balde_1,
  input  Abrir_Balde_2,
  input  Fechar_Balde_1,
  input  Stop,
  output \Lança_Elev__ou_Abai ,
  output Rodar_Esq__ou_Dir,
  output Enr__ou_Des__Cabo,
  output Abrir_ou_Fechar_Balde
);

  wire adder_1_out, adder_2_out, adder_3_out, adder_4_out, adder_5_out, adder_6_out, adder_7_out,
       adder_8_out, adder_9_out, adder_10_out, adder_11_out, adder_12_out, and_1_out, and_2_out, and_3_out,
       and_4_out;

  Adder #(.width(1)) adder_1 (.a(\Lança_Elev_1 ), .b(\Lança_Elev_2 ), .out(adder_1_out));  // open: cin, cout
  Adder #(.width(1)) adder_2 (.a(\Lança_Abai_1 ), .b(\Lança_Abai_2 ), .out(adder_2_out));  // open: cin, cout
  Adder #(.width(1)) adder_3 (.a(Rodar_Esq_1), .b(Rodar_Esq_2), .out(adder_3_out));  // open: cin, cout
  Adder #(.width(1)) adder_4 (.a(Rodar_Dir_1), .b(Rodar_Dir_2), .out(adder_4_out));  // open: cin, cout
  Adder #(.width(1)) adder_5 (.a(Cabo_Des_1), .b(Cabo_Des_2), .out(adder_5_out));  // open: cin, cout
  Adder #(.width(1)) adder_6 (.a(Cabo_Enr_1), .b(Cabo_Enr_2), .out(adder_6_out));  // open: cin, cout
  Adder #(.width(1)) adder_7 (.a(Abrir_Balde_1), .b(Abrir_Balde_2), .out(adder_7_out));  // open: cin, cout
  Adder #(.width(1)) adder_8 (.a(Stop), .b(Fechar_Balde_1), .out(adder_8_out));  // open: cin, cout
  Adder #(.width(1)) adder_9 (.a(adder_1_out), .b(adder_2_out), .out(adder_9_out));  // open: cin, cout
  Adder #(.width(1)) adder_10 (.a(adder_3_out), .b(adder_4_out), .out(adder_10_out));  // open: cin, cout
  Adder #(.width(1)) adder_11 (.a(adder_5_out), .b(adder_6_out), .out(adder_11_out));  // open: cin, cout
  Adder #(.width(1)) adder_12 (.a(adder_7_out), .b(adder_8_out), .out(adder_12_out));  // open: cin, cout
  and and_1 (and_1_out, adder_9_out, Stop);
  and and_2 (and_2_out, adder_10_out, Stop);
  and and_3 (and_3_out, adder_11_out, Stop);
  and and_4 (and_4_out, adder_12_out, Stop);
  nor nor_1 (\Lança_Elev__ou_Abai , and_1_out, and_2_out);
  nor nor_2 (Abrir_ou_Fechar_Balde, and_3_out, and_4_out);

  assign Enr__ou_Des__Cabo = Abrir_ou_Fechar_Balde;
  assign Rodar_Esq__ou_Dir = \Lança_Elev__ou_Abai ;
endmodule
