// Logisim project display 7segmentos.circ as structural Verilog: 1 circuit, main circuit main
module main (
  input  in_1,
  input  in_2,
  input  in_3,
  input  in_4
);

  wire and_1_out, and_2_out, and_3_out, and_4_out, and_5_out, and_6_out, and_7_out, and_8_out, and_9_out,
       and_10_out, and_11_out, and_12_out, and_13_out, and_14_out, and_15_out, and_16_out, and_17_out,
       and_18_out, and_19_out, and_20_out, and_21_out, and_22_out, and_23_out, and_24_out, and_25_out,
       and_26_out, and_27_out, and_28_out, and_29_out, and_30_out, and_31_out, and_32_out, and_33_out,
       and_34_out, and_35_out, and_36_out, and_37_out, not_1_out, not_2_out, not_3_out, not_4_out, or_1_out,
       or_2_out, or_3_out, or_4_out, or_5_out, or_6_out, or_7_out, or_8_out, or_9_out, or_10_out, or_11_out,
       or_12_out, or_13_out, or_14_out, or_15_out, or_16_out, or_17_out, or_18_out, or_19_out, or_20_out,
       or_21_out;

  not not_1 (not_1_out, in_1);
  not not_2 (not_2_out, in_2);
  not not_3 (not_3_out, in_3);
  not not_4 (not_4_out, in_4);
  and and_1 (and_1_out, not_1_out, not_3_out, not_4_out);
  and and_2 (and_2_out, not_1_out, in_3, in_4);
  and and_3 (and_3_out, in_1, not_3_out, in_4);
  and and_4 (and_4_out, not_2_out, not_3_out);
  and and_5 (and_5_out, not_2_out, in_3, not_4_out);
  and and_6 (and_6_out, not_2_out, not_3_out);
  and and_7 (and_7_out, not_1_out, in_4);
  and and_8 (and_8_out, not_1_out, in_2, not_4_out);
  and and_9 (and_9_out, in_1, not_3_out, in_4);
  and and_10 (and_10_out, in_1, not_2_out, in_3);
  and and_11 (and_11_out, in_1, not_2_out, not_3_out);
  and and_12 (and_12_out, not_1_out, in_2, in_4);
  and and_13 (and_13_out, not_1_out, in_3);
  and and_14 (and_14_out, in_1, not_4_out);
  and and_15 (and_15_out, not_2_out, not_4_out);
  and and_16 (and_16_out, in_2, in_3);
  or or_1 (or_1_out, and_6_out, and_7_out);
  or or_2 (or_2_out, and_8_out, and_9_out, and_10_out);
  or or_3 (or_3_out, and_11_out, and_12_out, and_13_out);
  or or_4 (or_4_out, and_14_out, and_15_out, and_16_out);
  or or_5 (or_5_out, and_1_out, and_2_out);
  or or_6 (or_6_out, and_3_out, and_4_out, and_5_out);
  or or_7 (or_7_out, or_3_out, or_4_out);
  or or_8 (or_8_out, or_5_out, or_6_out);
  or or_9 (or_9_out, or_1_out, or_2_out);
  or or_10 (or_10_out, and_18_out, and_17_out, and_19_out);
  and and_17 (and_17_out, not_1_out, in_2, not_3_out);
  and and_18 (and_18_out, not_1_out, not_2_out, in_3);
  _7_Segment_Display u_7_segment_display_1 (
    .g(or_11_out), .f(or_15_out), .a(or_7_out), .b(or_8_out), .e(or_12_out), .d(or_14_out), .c(or_9_out));  // open: dp
  or or_11 (or_11_out, or_10_out, or_13_out);
  and and_19 (and_19_out, in_2, in_3, not_4_out);
  or or_12 (or_12_out, or_18_out, or_19_out);
  or or_13 (or_13_out, and_20_out, and_21_out);
  and and_20 (and_20_out, in_1, not_2_out, not_4_out);
  or or_14 (or_14_out, or_16_out, or_17_out);
  or or_15 (or_15_out, or_20_out, or_21_out);
  and and_21 (and_21_out, in_1, in_4);
  or or_16 (or_16_out, and_22_out, and_23_out);
  or or_17 (or_17_out, and_24_out, and_25_out, and_26_out);
  or or_18 (or_18_out, and_27_out, and_28_out);
  or or_19 (or_19_out, and_29_out, and_30_out, and_31_out);
  or or_20 (or_20_out, and_32_out, and_33_out, and_34_out);
  or or_21 (or_21_out, and_35_out, and_36_out, and_37_out);
  and and_22 (and_22_out, in_2, not_3_out, in_4);
  and and_23 (and_23_out, not_2_out, in_3, in_4);
  and and_24 (and_24_out, not_2_out, not_3_out, not_4_out);
  and and_25 (and_25_out, not_1_out, in_3, not_4_out);
  and and_26 (and_26_out, in_1, in_2, not_4_out);
  and and_27 (and_27_out, not_2_out, not_4_out);
  and and_28 (and_28_out, in_1, not_4_out);
  and and_29 (and_29_out, in_2, in_3, not_4_out);
  and and_30 (and_30_out, in_1, in_2, in_4);
  and and_31 (and_31_out, in_1, in_3, in_4);
  and and_32 (and_32_out, not_1_out, in_2, not_3_out);
  and and_33 (and_33_out, not_1_out, not_3_out, not_4_out);
  and and_34 (and_34_out, in_1, not_2_out, not_3_out);
  and and_35 (and_35_out, in_1, in_3);
  and and_36 (and_36_out, in_2, in_3, not_4_out);
  and and_37 (and_37_out, in_1, in_2, not_4_out);

  // Notes on the sheet:
  //   C
  //   A
  //   B
  //   G
  //   D
  //   E
  //   F
endmodule
